// Logisim project hw4.circ as structural Verilog: 35 circuits, main circuit main
module main (
);

  wire clk, instructiondecode_1_chooseimmediate, instructiondecode_1_rtdestination,
       instructiondecode_1_writeenable, not_1_out;
  wire [2:0] instructiondecode_1_alufunction, instructiondecode_1_rd, instructiondecode_1_rs,
       instructiondecode_1_rt, multiplexer_1_out;
  wire [5:0] instructiondecode_1_immediate;
  wire [15:0] alu_1_result, instructionmemory_1_data, multiplexer_2_out, n1adder_1_output, pc_1_out,
       registerfile_1_readval1, registerfile_1_readval2, signextender_1_result;

  Clock clock_1 (.out(clk));
  PC pc_1 (.clk(clk), .\input (n1adder_1_output), .out(pc_1_out));
  _1adder u_1adder_1 (.\input (pc_1_out), .\output (n1adder_1_output));
  // Probe on instructionmemory_1_data
  InstructionMemory instructionmemory_1 (.address(pc_1_out), .data(instructionmemory_1_data));
  instructiondecode instructiondecode_1 (
    .instruction(instructionmemory_1_data), .rs(instructiondecode_1_rs), .rt(instructiondecode_1_rt),
    .rd(instructiondecode_1_rd), .immediate(instructiondecode_1_immediate),
    .aluFunction(instructiondecode_1_alufunction), .writeEnable(instructiondecode_1_writeenable),
    .chooseImmediate(instructiondecode_1_chooseimmediate), .rtDestination(instructiondecode_1_rtdestination));
  not not_1 (not_1_out, clk);
  // Probe on multiplexer_1_out
  Multiplexer #(.width(3)) multiplexer_1 (
    .in0(instructiondecode_1_rd), .in1(instructiondecode_1_rt), .out(multiplexer_1_out),
    .sel(instructiondecode_1_rtdestination));  // open: en
  // Probe on instructiondecode_1_rs
  // Probe on instructiondecode_1_rt
  // Probe on registerfile_1_readval1
  // Probe on multiplexer_2_out
  RegisterFile registerfile_1 (
    .clk(not_1_out), .RegisterDestination(multiplexer_1_out), .WriteEnable(instructiondecode_1_writeenable),
    .WriteVal(alu_1_result), .ReadInput1(instructiondecode_1_rs), .ReadInput2(instructiondecode_1_rt),
    .ReadVal1(registerfile_1_readval1), .ReadVal2(registerfile_1_readval2));
  signextender signextender_1 (.immediate(instructiondecode_1_immediate), .result(signextender_1_result));
  // Probe on signextender_1_result
  Multiplexer #(.width(16)) multiplexer_2 (
    .in0(registerfile_1_readval2), .in1(signextender_1_result), .out(multiplexer_2_out),
    .sel(instructiondecode_1_chooseimmediate));  // open: en
  // Probe on instructiondecode_1_alufunction
  alu alu_1 (
    .A(registerfile_1_readval1), .B(multiplexer_2_out), .\function (instructiondecode_1_alufunction),
    .result(alu_1_result));  // open: branchCondition
  // Probe on alu_1_result
endmodule

module _16bitregister (
  input  clk,
  input  enable,
  input  [15:0] D,
  output [15:0] out_4
);

  D_Flip_Flop d_ff_1 (.clk(clk), .D(D[15]), .Q(out_4[15]), .en(enable));  // open: Qn, preset, reset
  D_Flip_Flop d_ff_2 (.clk(clk), .D(D[14]), .Q(out_4[14]), .en(enable));  // open: Qn, preset, reset
  D_Flip_Flop d_ff_3 (.clk(clk), .D(D[13]), .Q(out_4[13]), .en(enable));  // open: Qn, preset, reset
  D_Flip_Flop d_ff_4 (.clk(clk), .D(D[12]), .Q(out_4[12]), .en(enable));  // open: Qn, preset, reset
  D_Flip_Flop d_ff_5 (.clk(clk), .D(D[11]), .Q(out_4[11]), .en(enable));  // open: Qn, preset, reset
  D_Flip_Flop d_ff_6 (.clk(clk), .D(D[10]), .Q(out_4[10]), .en(enable));  // open: Qn, preset, reset
  D_Flip_Flop d_ff_7 (.clk(clk), .D(D[9]), .Q(out_4[9]), .en(enable));  // open: Qn, preset, reset
  D_Flip_Flop d_ff_8 (.clk(clk), .D(D[8]), .Q(out_4[8]), .en(enable));  // open: Qn, preset, reset
  D_Flip_Flop d_ff_9 (.clk(clk), .D(D[7]), .Q(out_4[7]), .en(enable));  // open: Qn, preset, reset
  D_Flip_Flop d_ff_10 (.clk(clk), .D(D[6]), .Q(out_4[6]), .en(enable));  // open: Qn, preset, reset
  D_Flip_Flop d_ff_11 (.clk(clk), .D(D[5]), .Q(out_4[5]), .en(enable));  // open: Qn, preset, reset
  D_Flip_Flop d_ff_12 (.clk(clk), .D(D[4]), .Q(out_4[4]), .en(enable));  // open: Qn, preset, reset
  D_Flip_Flop d_ff_13 (.clk(clk), .D(D[3]), .Q(out_4[3]), .en(enable));  // open: Qn, preset, reset
  D_Flip_Flop d_ff_14 (.clk(clk), .D(D[2]), .Q(out_4[2]), .en(enable));  // open: Qn, preset, reset
  D_Flip_Flop d_ff_15 (.clk(clk), .D(D[1]), .Q(out_4[1]), .en(enable));  // open: Qn, preset, reset
  D_Flip_Flop d_ff_16 (.clk(clk), .D(D[0]), .Q(out_4[0]), .en(enable));  // open: Qn, preset, reset

  // Other names for the same wires on the sheet: out[15:0] = out_4
endmodule

module onebitadder (
  input  a,
  input  b,
  input  cIn,
  output s,
  output COut
);

  wire and_1_out, and_2_out, and_3_out, and_4_out, xor_1_out, xor_2_out;

  and and_1 (and_1_out, a, cIn);
  and and_2 (and_2_out, a, b);
  and and_3 (and_3_out, b, cIn);
  and and_4 (and_4_out, a, a, b, cIn);
  xor xor_1 (xor_1_out, a, b);
  or or_1 (COut, and_1_out, and_2_out, and_3_out);
  xor xor_2 (xor_2_out, xor_1_out, cIn);
  or or_2 (s, and_4_out, xor_2_out);
endmodule

module twobitcircuit (
  input  [1:0] a,
  input  [1:0] b,
  input  Cin,
  output [1:0] s,
  output COut
);

  wire onebitadder_1_cout;

  onebitadder onebitadder_1 (.a(a[0]), .b(b[0]), .cIn(Cin), .s(s[0]), .COut(onebitadder_1_cout));
  onebitadder onebitadder_2 (.a(a[1]), .b(b[1]), .cIn(onebitadder_1_cout), .s(s[1]), .COut(COut));
endmodule

module fourbitadder (
  input  [3:0] a,
  input  [3:0] b,
  input  CIn,
  output [3:0] s,
  output COut
);

  wire twobitcircuit_1_cout;

  twobitcircuit twobitcircuit_1 (.a(a[1:0]), .b(b[1:0]), .Cin(CIn), .s(s[1:0]), .COut(twobitcircuit_1_cout));
  twobitcircuit twobitcircuit_2 (.a(a[3:2]), .b(b[3:2]), .Cin(twobitcircuit_1_cout), .s(s[3:2]), .COut(COut));
endmodule

module eighbitcircuit (
  input  [7:0] a,
  input  [7:0] b,
  input  CIn,
  output [7:0] s,
  output COut
);

  wire fourbitadder_1_cout;

  fourbitadder fourbitadder_1 (.a(a[3:0]), .b(b[3:0]), .CIn(CIn), .s(s[3:0]), .COut(fourbitadder_1_cout));
  fourbitadder fourbitadder_2 (.a(a[7:4]), .b(b[7:4]), .CIn(fourbitadder_1_cout), .s(s[7:4]), .COut(COut));
endmodule

module binput (
  input  [15:0] b,
  input  c,
  output [15:0] out_3
);

  xor xor_1 (out_3[0], b[0], c);
  xor xor_2 (out_3[1], b[1], c);
  xor xor_3 (out_3[2], b[2], c);
  xor xor_4 (out_3[3], b[3], c);
  xor xor_5 (out_3[4], b[4], c);
  xor xor_6 (out_3[5], b[5], c);
  xor xor_7 (out_3[6], b[6], c);
  xor xor_8 (out_3[7], b[7], c);
  xor xor_9 (out_3[8], b[8], c);
  xor xor_10 (out_3[9], b[9], c);
  xor xor_11 (out_3[10], b[10], c);
  xor xor_12 (out_3[11], c, b[11]);
  xor xor_13 (out_3[12], b[12], c);
  xor xor_14 (out_3[13], b[13], c);
  xor xor_15 (out_3[14], b[14], c);
  xor xor_16 (out_3[15], b[15], c);
endmodule

module sixteenbitadder (
  input  [15:0] A,
  input  [15:0] B,
  input  sub,
  output C,
  output [15:0] result
);

  wire eighbitcircuit_1_cout, fourbitadder_1_cout, onebitadder_1_cout, twobitcircuit_1_cout;
  wire [15:0] binput_1_out_3;

  binput binput_1 (.b(B), .c(sub), .out_3(binput_1_out_3));
  eighbitcircuit eighbitcircuit_1 (
    .a(A[7:0]), .b(binput_1_out_3[7:0]), .CIn(sub), .s(result[7:0]), .COut(eighbitcircuit_1_cout));
  fourbitadder fourbitadder_1 (
    .a(A[11:8]), .b(binput_1_out_3[11:8]), .CIn(eighbitcircuit_1_cout), .s(result[11:8]),
    .COut(fourbitadder_1_cout));
  twobitcircuit twobitcircuit_1 (
    .a(A[13:12]), .b(binput_1_out_3[13:12]), .Cin(fourbitadder_1_cout), .s(result[13:12]),
    .COut(twobitcircuit_1_cout));
  onebitadder onebitadder_1 (
    .a(A[14]), .b(binput_1_out_3[14]), .cIn(twobitcircuit_1_cout), .s(result[14]), .COut(onebitadder_1_cout));
  onebitadder onebitadder_2 (.a(A[15]), .b(binput_1_out_3[15]), .cIn(onebitadder_1_cout), .s(result[15]), .COut(C));

  // Other names for the same wires on the sheet: sum[15:0] = result
endmodule

module sll (
  input  [15:0] in,
  output [15:0] out
);


  assign out = {in[14:0], 1'b0};
endmodule

module srl (
  input  [15:0] in,
  output [15:0] out
);


  assign out = {1'b0, in[15:1]};
endmodule

module alu (
  input  [15:0] A,
  input  [15:0] B,
  input  [2:0] \function ,
  output branchCondition,
  output [15:0] result
);

  wire equalto_1_out_3, multiplexer_1_out, n3bitequalto_1_out_3, n3bitequalto_2_out_3, n3bitequalto_3_out_3,
       n16bitlessthan_1_out, not_1_out, or_1_out;
  wire [15:0] not_2_out, sixteenbitadder_1_result, sixteenbitadder_2_result, sll_1_out, srl_1_out, xor_1_out;

  sll sll_1 (.in(A), .out(sll_1_out));
  srl srl_1 (.in(A), .out(srl_1_out));
  equalto equalto_1 (.A(A), .B(B), .out_3(equalto_1_out_3));
  not not_1 (not_1_out, equalto_1_out_3);
  _16bitlessthan u_16bitlessthan_1 (.A(A), .B(B), .out(n16bitlessthan_1_out));
  sixteenbitadder sixteenbitadder_1 (.A(A), .B(B), .sub(1'b1), .result(sixteenbitadder_1_result));  // open: C
  assign not_2_out = ~A;  // NOT_Gate not_2, 16 bits wide
  assign xor_1_out = A ^ B;  // XOR_Gate xor_1, 16 bits wide
  _3bitequalto u_3bitequalto_1 (.A(3'b111), .B(\function ), .out_3(n3bitequalto_1_out_3));
  sixteenbitadder sixteenbitadder_2 (.A(A), .B(B), .sub(1'b0), .result(sixteenbitadder_2_result));  // open: C
  Multiplexer multiplexer_1 (
    .in0(not_1_out), .in1(n16bitlessthan_1_out), .out(multiplexer_1_out), .sel(n3bitequalto_1_out_3));  // open: en
  _3bitequalto u_3bitequalto_2 (.A(3'b110), .B(\function ), .out_3(n3bitequalto_2_out_3));
  _3bitequalto u_3bitequalto_3 (.A(3'b111), .B(\function ), .out_3(n3bitequalto_3_out_3));
  or or_1 (or_1_out, n3bitequalto_2_out_3, n3bitequalto_3_out_3);
  Multiplexer multiplexer_2 (.in0(1'b0), .in1(multiplexer_1_out), .out(branchCondition), .sel(or_1_out));  // open: en
  Multiplexer #(.select(3), .width(16)) multiplexer_3 (
    .in0(sixteenbitadder_2_result), .in1(sixteenbitadder_1_result), .in2(not_2_out), .in3(xor_1_out),
    .in4(sll_1_out), .in5(srl_1_out), .in6({16{1'b0}}), .in7({16{1'b0}}), .out(result), .sel(\function ));  // open: en
endmodule

module instructiondecode (
  input  [15:0] instruction,
  output [2:0] rs,
  output [2:0] rt,
  output [2:0] rd,
  output [5:0] immediate,
  output [2:0] aluFunction,
  output writeEnable,
  output chooseImmediate,
  output rtDestination
);

  wire [1:0] typeChoose;
  wire [2:0] itype_1_rs, itype_1_rt, rtype_1_rs, rtype_1_rt;

  // Probe on typeChoose
  typedecode typedecode_1 (.in_1(instruction[15:12]), .out_2(typeChoose));
  rtype rtype_1 (.info(instruction[11:0]), .rs(rtype_1_rs), .rt(rtype_1_rt), .rd(rd));  // open: shamt
  itype itype_1 (.info(instruction[11:0]), .rs(itype_1_rs), .rt(itype_1_rt), .immediate(immediate));
  Multiplexer #(.select(2), .width(3)) multiplexer_1 (
    .in0(rtype_1_rs), .in1(itype_1_rs), .out(rs), .sel(typeChoose));  // open: in2, in3, en
  Multiplexer #(.select(2), .width(3)) multiplexer_2 (
    .in0(rtype_1_rt), .in1(itype_1_rt), .out(rt), .sel(typeChoose));  // open: in2, in3, en
  instructionopcode instructionopcode_1 (
    .in_1(instruction[15:12]), .immediate(chooseImmediate), .rtDestination(rtDestination),
    .aluFunction(aluFunction), .writeEnable(writeEnable));
  eighbitcircuit eighbitcircuit_1 ();  // open: a, b, CIn, s, COut
  Multiplexer multiplexer_3 ();  // open: in0, in1, out, sel, en

  // Other names for the same wires on the sheet: opcode[3:0] = instruction[15:12]
endmodule

module signextender (
  input  [5:0] immediate,
  output [15:0] result
);


  assign result = {{11{immediate[5]}}, immediate[4:0]};
endmodule

module RegisterFile (
  input  clk,
  input  [2:0] RegisterDestination,
  input  WriteEnable,
  input  [15:0] WriteVal,
  input  [2:0] ReadInput1,
  input  [2:0] ReadInput2,
  output [15:0] ReadVal1,
  output [15:0] ReadVal2
);

  wire and_1_out, and_2_out, and_3_out, and_4_out, and_5_out, and_6_out, and_7_out, and_8_out,
       decoder_1_out0, decoder_1_out1, decoder_1_out2, decoder_1_out3, decoder_1_out4, decoder_1_out5,
       decoder_1_out6, decoder_1_out7, decoder_2_out0, decoder_2_out1, decoder_2_out2, decoder_2_out3,
       decoder_2_out4, decoder_2_out5, decoder_2_out6, decoder_2_out7, decoder_3_out0, decoder_3_out1,
       decoder_3_out2, decoder_3_out3, decoder_3_out4, decoder_3_out5, decoder_3_out6, decoder_3_out7;
  wire [15:0] n16bitregister_1_out_4, n16bitregister_2_out_4, n16bitregister_3_out_4, n16bitregister_4_out_4,
       n16bitregister_5_out_4, n16bitregister_6_out_4, n16bitregister_7_out_4, n16bitregister_8_out_4;

  and and_1 (and_1_out, 1'b0, decoder_3_out0);
  // Probe on n16bitregister_1_out_4
  Decoder #(.select(3)) decoder_1 (
    .out0(decoder_1_out0), .out1(decoder_1_out1), .out2(decoder_1_out2), .out3(decoder_1_out3),
    .out4(decoder_1_out4), .out5(decoder_1_out5), .out6(decoder_1_out6), .out7(decoder_1_out7),
    .sel(ReadInput1));  // open: en
  Decoder #(.select(3)) decoder_2 (
    .out0(decoder_2_out0), .out1(decoder_2_out1), .out2(decoder_2_out2), .out3(decoder_2_out3),
    .out4(decoder_2_out4), .out5(decoder_2_out5), .out6(decoder_2_out6), .out7(decoder_2_out7),
    .sel(ReadInput2));  // open: en
  Decoder #(.select(3)) decoder_3 (
    .out0(decoder_3_out0), .out1(decoder_3_out1), .out2(decoder_3_out2), .out3(decoder_3_out3),
    .out4(decoder_3_out4), .out5(decoder_3_out5), .out6(decoder_3_out6), .out7(decoder_3_out7),
    .sel(RegisterDestination));  // open: en
  _16bitregister u_16bitregister_1 (.clk(clk), .enable(and_1_out), .D(WriteVal), .out_4(n16bitregister_1_out_4));
  assign ReadVal2 = decoder_2_out0 ? n16bitregister_1_out_4 : 16'bz;  // Controlled_Buffer controlled_buffer_1
  and and_2 (and_2_out, decoder_3_out1, WriteEnable);
  _16bitregister u_16bitregister_2 (.clk(clk), .enable(and_2_out), .D(WriteVal), .out_4(n16bitregister_2_out_4));
  // Probe on n16bitregister_2_out_4
  assign ReadVal1 = decoder_1_out0 ? n16bitregister_1_out_4 : 16'bz;  // Controlled_Buffer controlled_buffer_2
  and and_3 (and_3_out, decoder_3_out2, WriteEnable, WriteEnable);
  _16bitregister u_16bitregister_3 (.clk(clk), .enable(and_3_out), .D(WriteVal), .out_4(n16bitregister_3_out_4));
  // Probe on n16bitregister_3_out_4
  assign ReadVal1 = decoder_1_out1 ? n16bitregister_2_out_4 : 16'bz;  // Controlled_Buffer controlled_buffer_3
  assign ReadVal2 = decoder_2_out1 ? n16bitregister_2_out_4 : 16'bz;  // Controlled_Buffer controlled_buffer_4
  and and_4 (and_4_out, decoder_3_out3, WriteEnable, WriteEnable);
  assign ReadVal1 = decoder_1_out2 ? n16bitregister_3_out_4 : 16'bz;  // Controlled_Buffer controlled_buffer_5
  assign ReadVal2 = decoder_2_out2 ? n16bitregister_3_out_4 : 16'bz;  // Controlled_Buffer controlled_buffer_6
  and and_5 (and_5_out, decoder_3_out4, WriteEnable);
  _16bitregister u_16bitregister_4 (.clk(clk), .enable(and_4_out), .D(WriteVal), .out_4(n16bitregister_4_out_4));
  // Probe on n16bitregister_4_out_4
  assign ReadVal1 = decoder_1_out3 ? n16bitregister_4_out_4 : 16'bz;  // Controlled_Buffer controlled_buffer_7
  assign ReadVal2 = decoder_2_out3 ? n16bitregister_4_out_4 : 16'bz;  // Controlled_Buffer controlled_buffer_8
  and and_6 (and_6_out, decoder_3_out5, WriteEnable, WriteEnable, WriteEnable);
  _16bitregister u_16bitregister_5 (.clk(clk), .enable(and_5_out), .D(WriteVal), .out_4(n16bitregister_5_out_4));
  // Probe on n16bitregister_5_out_4
  assign ReadVal1 = decoder_1_out4 ? n16bitregister_5_out_4 : 16'bz;  // Controlled_Buffer controlled_buffer_9
  assign ReadVal2 = decoder_2_out4 ? n16bitregister_5_out_4 : 16'bz;  // Controlled_Buffer controlled_buffer_10
  _16bitregister u_16bitregister_6 (.clk(clk), .enable(and_6_out), .D(WriteVal), .out_4(n16bitregister_6_out_4));
  // Probe on n16bitregister_6_out_4
  and and_7 (and_7_out, decoder_3_out6, WriteEnable, WriteEnable);
  assign ReadVal1 = decoder_1_out5 ? n16bitregister_6_out_4 : 16'bz;  // Controlled_Buffer controlled_buffer_11
  assign ReadVal2 = decoder_2_out5 ? n16bitregister_6_out_4 : 16'bz;  // Controlled_Buffer controlled_buffer_12
  and and_8 (and_8_out, decoder_3_out7, WriteEnable);
  _16bitregister u_16bitregister_7 (.clk(clk), .enable(and_7_out), .D(WriteVal), .out_4(n16bitregister_7_out_4));
  // Probe on n16bitregister_7_out_4
  assign ReadVal1 = decoder_1_out6 ? n16bitregister_7_out_4 : 16'bz;  // Controlled_Buffer controlled_buffer_13
  assign ReadVal2 = decoder_2_out6 ? n16bitregister_7_out_4 : 16'bz;  // Controlled_Buffer controlled_buffer_14
  _16bitregister u_16bitregister_8 (.clk(clk), .enable(and_8_out), .D(WriteVal), .out_4(n16bitregister_8_out_4));
  // Probe on n16bitregister_8_out_4
  assign ReadVal2 = decoder_2_out7 ? n16bitregister_8_out_4 : 16'bz;  // Controlled_Buffer controlled_buffer_15
  assign ReadVal1 = decoder_1_out7 ? n16bitregister_8_out_4 : 16'bz;  // Controlled_Buffer controlled_buffer_16
endmodule

module DataMemory (
  input  [15:0] data,
  input  writeenable,
  input  [15:0] address,
  input  clk,
  output [15:0] \output 
);

  wire not_1_out;

  assign \output  = writeenable ? data : 16'bz;  // Controlled_Buffer controlled_buffer_1
  not not_1 (not_1_out, writeenable);
  RAM #(.addrWidth(16), .dataWidth(16)) ram_1 (
    .addr(address), .data(\output ), .clk(clk), .ld(not_1_out));  // open: sel, clr
endmodule

module InstructionMemory (
  input  [15:0] address,
  output [15:0] data
);

  ROM #(.addrWidth(16), .dataWidth(16)) rom_1 (.addr(address), .data(data));  // open: sel

  // Notes on the sheet:
  //   contents of rom_1 (hex, n*v repeats v):
  //   1102 15*968 9*2b28 3a00 3000
endmodule

module PC (
  input  clk,
  input  [15:0] \input ,
  output [15:0] out
);

  _16bitregister u_16bitregister_1 (.clk(clk), .enable(1'b1), .D(\input ), .out_4(out));
endmodule

module _1adder (
  input  [15:0] \input ,
  output [15:0] \output 
);

  sixteenbitadder sixteenbitadder_1 (.A(\input ), .B(16'h1), .sub(1'b0), .result(\output ));  // open: C
endmodule

module _12bitsignextender (
  input  [11:0] in,
  output [15:0] out
);


  assign out = {4'b0000, in};
endmodule

module _12bitsll (
  input  [11:0] in,
  output [11:0] out
);


  assign out = {in[10:0], 1'b0};
endmodule

module equalto (
  input  [15:0] A,
  input  [15:0] B,
  output out_3
);

  wire and_1_out, and_2_out, and_3_out, and_4_out, and_5_out, and_6_out, and_7_out, and_8_out, and_9_out,
       and_10_out, and_11_out, and_12_out, and_13_out, and_14_out, xnor_1_out, xnor_2_out, xnor_3_out,
       xnor_4_out, xnor_5_out, xnor_6_out, xnor_7_out, xnor_8_out, xnor_9_out, xnor_10_out, xnor_11_out,
       xnor_12_out, xnor_13_out, xnor_14_out, xnor_15_out, xnor_16_out;

  xnor xnor_1 (xnor_1_out, A[0], B[0]);
  xnor xnor_2 (xnor_2_out, A[1], B[1]);
  xnor xnor_3 (xnor_3_out, A[2], B[2]);
  xnor xnor_4 (xnor_4_out, A[3], B[3]);
  xnor xnor_5 (xnor_5_out, A[4], B[4]);
  xnor xnor_6 (xnor_6_out, A[5], B[5]);
  xnor xnor_7 (xnor_7_out, A[6], B[6]);
  xnor xnor_8 (xnor_8_out, A[7], B[7]);
  xnor xnor_9 (xnor_9_out, A[8], B[8]);
  xnor xnor_10 (xnor_10_out, A[9], B[9]);
  xnor xnor_11 (xnor_11_out, A[10], B[10]);
  xnor xnor_12 (xnor_12_out, A[11], B[11]);
  xnor xnor_13 (xnor_13_out, A[12], B[12]);
  xnor xnor_14 (xnor_14_out, A[13], B[13]);
  xnor xnor_15 (xnor_15_out, B[14], B[14]);
  and and_1 (and_1_out, xnor_1_out, xnor_2_out);
  xnor xnor_16 (xnor_16_out, A[15], B[15]);
  and and_2 (and_2_out, xnor_3_out, xnor_4_out);
  and and_3 (and_3_out, xnor_5_out, xnor_5_out, xnor_6_out, xnor_6_out);
  and and_4 (and_4_out, xnor_7_out, xnor_8_out);
  and and_5 (and_5_out, xnor_9_out, xnor_10_out);
  and and_6 (and_6_out, xnor_11_out, xnor_12_out);
  and and_7 (and_7_out, xnor_13_out, xnor_14_out, xnor_14_out);
  and and_8 (and_8_out, xnor_15_out, xnor_16_out);
  and and_9 (and_9_out, and_1_out, and_2_out);
  and and_10 (and_10_out, and_3_out, and_4_out);
  and and_11 (and_11_out, and_5_out, and_5_out, and_6_out);
  and and_12 (and_12_out, and_7_out, and_8_out);
  and and_13 (and_13_out, and_9_out, and_10_out);
  and and_14 (and_14_out, and_11_out, and_12_out);
  and and_15 (out_3, and_13_out, and_14_out);
endmodule

module _1bitlessthan (
  input  A,
  input  B,
  output out
);

  wire not_1_out;

  not not_1 (not_1_out, A);
  and and_1 (out, not_1_out, B);
endmodule

module _2bitlessthan (
  input  [1:0] in_1,
  input  [1:0] in_2,
  output out_3
);

  wire and_1_out, n1bitlessthan_1_out, n1bitlessthan_2_out, xnor_1_out;

  _1bitlessthan u_1bitlessthan_1 (.A(in_1[0]), .B(in_2[0]), .out(n1bitlessthan_1_out));
  _1bitlessthan u_1bitlessthan_2 (.A(in_1[1]), .B(in_2[1]), .out(n1bitlessthan_2_out));
  xnor xnor_1 (xnor_1_out, in_1[1], in_2[1]);
  and and_1 (and_1_out, xnor_1_out, n1bitlessthan_1_out);
  or or_1 (out_3, n1bitlessthan_2_out, and_1_out);
endmodule

module _3bitlessthan (
  input  [2:0] A,
  input  [2:0] B,
  output out_3
);

  wire and_1_out, n1bitlessthan_1_out, n2bitlessthan_1_out_3, xnor_1_out;

  _2bitlessthan u_2bitlessthan_1 (.in_1(A[1:0]), .in_2(B[1:0]), .out_3(n2bitlessthan_1_out_3));
  xnor xnor_1 (xnor_1_out, A[2], B[2]);
  and and_1 (and_1_out, n2bitlessthan_1_out_3, xnor_1_out);
  _1bitlessthan u_1bitlessthan_1 (.A(A[2]), .B(B[2]), .out(n1bitlessthan_1_out));
  or or_1 (out_3, and_1_out, n1bitlessthan_1_out);
endmodule

module _4bitlessthan (
  input  [3:0] in_1,
  input  [3:0] in_2,
  output out_3
);

  wire and_1_out, n1bitlessthan_1_out, n3bitlessthan_1_out_3, xnor_1_out;

  _3bitlessthan u_3bitlessthan_1 (.A(in_1[2:0]), .B(in_2[2:0]), .out_3(n3bitlessthan_1_out_3));
  _1bitlessthan u_1bitlessthan_1 (.A(in_1[3]), .B(in_2[3]), .out(n1bitlessthan_1_out));
  xnor xnor_1 (xnor_1_out, in_1[3], in_2[3]);
  and and_1 (and_1_out, n3bitlessthan_1_out_3, xnor_1_out);
  or or_1 (out_3, and_1_out, n1bitlessthan_1_out);
endmodule

module _4bitequalto (
  input  [3:0] A,
  input  [3:0] B,
  output out
);

  wire xnor_1_out, xnor_2_out, xnor_3_out, xnor_4_out;

  xnor xnor_1 (xnor_1_out, A[0], B[0]);
  xnor xnor_2 (xnor_2_out, A[1], B[1]);
  xnor xnor_3 (xnor_3_out, A[2], B[2]);
  xnor xnor_4 (xnor_4_out, A[3], B[3]);
  and and_1 (out, xnor_1_out, xnor_2_out, xnor_3_out, xnor_4_out);
endmodule

module _8bitlessthan (
  input  [7:0] A,
  input  [7:0] B,
  output out
);

  wire and_1_out, n4bitequalto_1_out, n4bitlessthan_1_out_3, n4bitlessthan_2_out_3;

  _4bitlessthan u_4bitlessthan_1 (.in_1(A[7:4]), .in_2(B[7:4]), .out_3(n4bitlessthan_1_out_3));
  _4bitlessthan u_4bitlessthan_2 (.in_1(A[3:0]), .in_2(B[3:0]), .out_3(n4bitlessthan_2_out_3));
  _4bitequalto u_4bitequalto_1 (.A(A[7:4]), .B(B[7:4]), .out(n4bitequalto_1_out));
  and and_1 (and_1_out, n4bitlessthan_2_out_3, n4bitequalto_1_out);
  or or_1 (out, n4bitlessthan_1_out_3, and_1_out);
endmodule

module _8bitequalto (
  input  [7:0] A,
  input  [7:0] B,
  output out_3
);

  wire n4bitequalto_1_out, n4bitequalto_2_out;

  _4bitequalto u_4bitequalto_1 (.A(A[3:0]), .B(B[3:0]), .out(n4bitequalto_1_out));
  _4bitequalto u_4bitequalto_2 (.A(A[7:4]), .B(B[7:4]), .out(n4bitequalto_2_out));
  and and_1 (out_3, n4bitequalto_1_out, n4bitequalto_2_out);
endmodule

module _16bitlessthan (
  input  [15:0] A,
  input  [15:0] B,
  output out
);

  wire and_1_out, n8bitequalto_1_out_3, n8bitlessthan_1_out, n8bitlessthan_2_out;

  _8bitlessthan u_8bitlessthan_1 (.A(A[15:8]), .B(B[15:8]), .out(n8bitlessthan_1_out));
  _8bitlessthan u_8bitlessthan_2 (.A(A[7:0]), .B(B[7:0]), .out(n8bitlessthan_2_out));
  _8bitequalto u_8bitequalto_1 (.A(B[15:8]), .B(A[15:8]), .out_3(n8bitequalto_1_out_3));
  and and_1 (and_1_out, n8bitequalto_1_out_3, n8bitlessthan_2_out);
  or or_1 (out, n8bitlessthan_1_out, and_1_out);
endmodule

module _3bitequalto (
  input  [2:0] A,
  input  [2:0] B,
  output out_3
);

  wire xnor_1_out, xnor_2_out, xnor_3_out;

  xnor xnor_1 (xnor_1_out, A[0], B[0]);
  xnor xnor_2 (xnor_2_out, A[1], B[1]);
  xnor xnor_3 (xnor_3_out, A[2], B[2]);
  and and_1 (out_3, xnor_1_out, xnor_2_out, xnor_3_out);
endmodule

module rtype (
  input  [11:0] info,
  output [2:0] rs,
  output [2:0] rt,
  output [2:0] rd,
  output [2:0] shamt
);


  assign rd = info[5:3];
  assign rs = info[11:9];
  assign rt = info[8:6];
  assign shamt = info[2:0];
endmodule

module itype (
  input  [11:0] info,
  output [2:0] rs,
  output [2:0] rt,
  output [5:0] immediate
);


  assign immediate = info[5:0];
  assign rs = info[11:9];
  assign rt = info[8:6];
endmodule

module instructionopcode (
  input  [3:0] in_1,
  output immediate,
  output rtDestination,
  output [2:0] aluFunction,
  output writeEnable
);

  wire decoder_1_out0, decoder_1_out2, decoder_1_out3, decoder_1_out4, decoder_1_out5, decoder_1_out6,
       decoder_1_out7, decoder_1_out8, decoder_1_out9, decoder_1_out10, decoder_1_out11, decoder_1_out12,
       decoder_1_out13, decoder_1_out14, decoder_1_out15;

  Decoder #(.select(4)) decoder_1 (
    .out0(decoder_1_out0), .out1(immediate), .out2(decoder_1_out2), .out3(decoder_1_out3),
    .out4(decoder_1_out4), .out5(decoder_1_out5), .out6(decoder_1_out6), .out7(decoder_1_out7),
    .out8(decoder_1_out8), .out9(decoder_1_out9), .out10(decoder_1_out10), .out11(decoder_1_out11),
    .out12(decoder_1_out12), .out13(decoder_1_out13), .out14(decoder_1_out14), .out15(decoder_1_out15),
    .sel(in_1));  // open: en
  or or_1 (writeEnable, decoder_1_out0, immediate, decoder_1_out2);
  Multiplexer #(.select(4), .width(3)) multiplexer_1 (
    .in0(3'b000), .in1(3'b000), .in2(3'b001), .in3(3'b010), .out(aluFunction), .sel(in_1));  // open: in4, in5, in6, in7, in8, in9, in10, in11, in12, in13, in14, in15, en

  assign rtDestination = immediate;
endmodule

module mainbackup (
  input  branching,
  input  jumping,
  input  jump_to_register,
  input  [2:0] rd,
  input  loading,
  input  datawriteenable,
  input  chooseimmediage,
  input  destinationchoose,
  input  writeenable,
  input  [5:0] immediatevalue,
  input  [2:0] functionchoose,
  input  [2:0] rs,
  input  [2:0] rt,
  input  [11:0] jimmediate
);

  wire alu_1_p4, and_1_out, clk;
  wire [2:0] multiplexer_1_out;
  wire [15:0] alu_1_p5, datamemory_1_output, instructionmemory_1_data, multiplexer_2_out, multiplexer_3_out,
       multiplexer_4_out, multiplexer_5_out, n1adder_1_output, n12bitsignextender_1_out, pc_1_out,
       registerfile_1_p4, registerfile_1_p7, registerfile_1_p8, signextender_1_result,
       sixteenbitadder_1_result, sll_1_out, sll_2_out;

  PC pc_1 (.clk(clk), .\input (multiplexer_5_out), .out(pc_1_out));
  _1adder u_1adder_1 (.\input (pc_1_out), .\output (n1adder_1_output));
  InstructionMemory instructionmemory_1 (.address(pc_1_out), .data(instructionmemory_1_data));
  Keyboard keyboard_1 ();  // open: clk, re, clr, avail, data
  Clock clock_1 (.out(clk));
  Multiplexer #(.width(3)) multiplexer_1 (
    .in0(rd), .in1(rt), .out(multiplexer_1_out), .sel(destinationchoose));  // open: en
  // RegisterFile registerfile_1: pin names not known; wires that end beside it: multiplexer_1_out, writeenable, clk, registerfile_1_p4, rs, rt, registerfile_1_p7, registerfile_1_p8
  _12bitsignextender u_12bitsignextender_1 (.in(jimmediate), .out(n12bitsignextender_1_out));
  Multiplexer #(.width(16)) multiplexer_2 (
    .in0(n12bitsignextender_1_out), .in1(registerfile_1_p7), .out(multiplexer_2_out), .sel(jump_to_register));  // open: en
  signextender signextender_1 (.immediate(immediatevalue), .result(signextender_1_result));
  sll sll_1 (.in(signextender_1_result), .out(sll_1_out));
  sll sll_2 (.in(multiplexer_2_out), .out(sll_2_out));
  Multiplexer #(.width(16)) multiplexer_3 (
    .in0(registerfile_1_p8), .in1(signextender_1_result), .out(multiplexer_3_out), .sel(chooseimmediage));  // open: en
  TTY tty_1 ();  // open: data, clk, we, clr
  // alu alu_1: pin names not known; wires that end beside it: multiplexer_3_out, functionchoose, registerfile_1_p7, alu_1_p4, alu_1_p5
  sixteenbitadder sixteenbitadder_1 (
    .A(n1adder_1_output), .B(sll_1_out), .sub(1'b0), .result(sixteenbitadder_1_result));  // open: C
  and and_1 (and_1_out, branching, alu_1_p4);
  Multiplexer #(.width(16)) multiplexer_4 (
    .in0(n1adder_1_output), .in1(sixteenbitadder_1_result), .out(multiplexer_4_out), .en(and_1_out));  // open: sel
  DataMemory datamemory_1 (
    .data(registerfile_1_p8), .writeenable(datawriteenable), .address(alu_1_p5), .clk(clk),
    .\output (datamemory_1_output));
  Multiplexer #(.width(16)) multiplexer_5 (
    .in0(multiplexer_4_out), .in1(sll_2_out), .out(multiplexer_5_out), .en(jumping));  // open: sel
  Multiplexer #(.width(16)) multiplexer_6 (
    .in0(alu_1_p5), .in1(datamemory_1_output), .out(registerfile_1_p4), .en(loading));  // open: sel
endmodule

module typedecode (
  input  [3:0] in_1,
  output [1:0] out_2
);

  wire n4bitequalto_1_out;

  _4bitequalto u_4bitequalto_1 (.A(in_1), .B(4'b0001), .out(n4bitequalto_1_out));
  Multiplexer #(.width(2)) multiplexer_1 (.in0(2'b00), .in1(2'b01), .out(out_2), .sel(n4bitequalto_1_out));  // open: en
endmodule
